# Fritzing sketch FlexRigShield2026 (saved by Fritzing 0.9.6b)
circuit board: 9.79981cm x 5.71769cm
breadboards: 1

parts:
  1MΩ = Resistor [tolerance=±5% resistance=1M power=0.25 package=THT]
  1MΩ_2 = Resistor [tolerance=±5% resistance=1M power=0.25 package=THT]
  1MΩ_3 = Resistor [tolerance=±5% resistance=1M power=0.25 package=THT]
  1MΩ_4 = Resistor [tolerance=±5% resistance=1M power=0.25 package=THT]
  1MΩ_5 = Resistor [tolerance=±5% resistance=1M power=0.25 package=THT]
  1MΩ_6 = Resistor [tolerance=±5% resistance=1M power=0.25 package=THT]
  1MΩ_7 = Resistor [tolerance=±5% resistance=1M power=0.25 package=THT]
  1MΩ_8 = Resistor [tolerance=±5% resistance=1M power=0.25 package=THT]
  part = female pin header, 6 pins [form="♀ (female)"]
  part_2 = female pin header, 6 pins [form="♀ (female)"]  # not connected
  part_3 = female pin header, 8 pins [form="♀ (female)"]
  part_4 = female pin header, 8 pins [form="♀ (female)"]
  1MΩ_9 = Resistor [tolerance=±5% resistance=1M power=0.25 package=THT]
  part_5 = female pin header, 2 pins [form="♀ (female)"]
  part_6 = female pin header, 2 pins [form="♀ (female)"]
  part_7 = female pin header, 2 pins [form="♀ (female)"]
  part_8 = female pin header, 2 pins [form="♀ (female)"]
  part_9 = female pin header, 2 pins [form="♀ (female)"]
  part_10 = female pin header, 2 pins [form="♀ (female)"]
  SN75441ONE = H-Bridge [package=THT]
  SN75441ONE_2 = H-Bridge [package=THT]
  1MΩ_10 = Resistor [tolerance=±5% resistance=1M power=0.25 package=THT]
  1MΩ_11 = Resistor [tolerance=±5% resistance=1M power=0.25 package=THT]
  A0_A5 = FTDI_BASIC [package=ftdi_basic]
  R_3_5_G_G_V = FTDI_BASIC [package=ftdi_basic]
  1MΩ_12 = Resistor [tolerance=±5% power=0.25 resistance=100k package=THT]
  part_11 = female pin header, 2 pins [form="♀ (female)"]
  reset = SWITCH-MOMENTARY-2 [package=tactile-switch-1101ne]
  part_12 = female pin header, 8 pins [form="♀ (female)"]
  FlexRig = double row female pin header, 36 pins [form="♀ (female)"]
  part_13 = female pin header, 8 pins [form="♀ (female)"]  # not connected

nets:
  GND1: 1MΩ.Pin_0, 1MΩ_2.Pin_0, 1MΩ_3.Pin_0, 1MΩ_4.Pin_0, 1MΩ_6.Pin_0, 1MΩ_7.Pin_0, 1MΩ_8.Pin_0, part.pin2, 1MΩ_9.Pin_0, part_5.pin2, part_6.pin2, part_7.pin2, part_8.pin2, part_9.pin2, part_10.pin2, SN75441ONE.GND1, SN75441ONE.GND2, SN75441ONE.GND3, SN75441ONE.GND4, SN75441ONE_2.GND1, SN75441ONE_2.GND2, SN75441ONE_2.GND3, SN75441ONE_2.GND4, 1MΩ_10.Pin_1, 1MΩ_11.Pin_1, R_3_5_G_G_V.5, R_3_5_G_G_V.4, 1MΩ_12.Pin_1, reset.1
  N1: 1MΩ.Pin_1, part_4.pin2, SN75441ONE_2.2A
  N2: 1MΩ_2.Pin_1, part_3.pin8, SN75441ONE.3A
  N3: 1MΩ_3.Pin_1, part_3.pin6, SN75441ONE.1A
  N4: 1MΩ_4.Pin_1, part_3.pin5, SN75441ONE.4A
  N5: 1MΩ_5.Pin_1, R_3_5_G_G_V.2
  N6: 1MΩ_6.Pin_1, part_4.pin3, SN75441ONE_2.1A
  N7: 1MΩ_7.Pin_1, part_3.pin7
  N8: 1MΩ_8.Pin_1, part_4.pin1, SN75441ONE_2.4A
  N9: part.pin1, FlexRig.pin1
  N10: part.pin3, part_12.pin5
  N11: part.pin4, part_12.pin6
  N12: part_4.pin4, 1MΩ_9.Pin_1
  N13: part_4.pin5, SN75441ONE.2A
  N14: part_4.pin6, SN75441ONE_2.3A
  N15: part_5.pin1, SN75441ONE.4Y
  N16: part_6.pin1, SN75441ONE.1Y
  N17: part_7.pin1, SN75441ONE.3Y
  N18: part_8.pin1, SN75441ONE_2.1Y
  N19: part_9.pin1, SN75441ONE_2.4Y
  N20: part_10.pin1, SN75441ONE_2.2Y
  N21: SN75441ONE.1_2EN, SN75441ONE.VCC1, SN75441ONE_2.1_2EN, SN75441ONE_2.VCC1, R_3_5_G_G_V.3
  N22: SN75441ONE.VCC2, SN75441ONE_2.VCC2, R_3_5_G_G_V.6
  N23: SN75441ONE.3_4EN, SN75441ONE_2.3_4EN
  N24: 1MΩ_10.Pin_0, A0_A5.6
  N25: 1MΩ_11.Pin_0, A0_A5.1
  N26: R_3_5_G_G_V.1, reset.2
  N27: 1MΩ_12.Pin_0, part_11.pin1
